// Logisim project project-5-gudbrand.circ as structural Verilog: 15 circuits, main circuit main
module main (
  input  CLR
);

  wire CLK, control_unit_1_alusrc, control_unit_1_memtoreg, control_unit_1_memwrite, control_unit_1_pcsrc,
       control_unit_1_regwrite;
  wire [1:0] control_unit_1_alucontrol, control_unit_1_immsrc, control_unit_1_regsrc;
  wire [3:0] alu_1_alu_flags, multiplexer_2_out, multiplexer_3_out;
  wire [31:0] adder_2_out, alu_1_result, data_memory_1_rd, extend_1_extimm, instruction_memory_1_out_2,
       multiplexer_1_out, multiplexer_4_out, multiplexer_5_out, R0, R1, R2, R3, R4, R5, R6, R7, R8, R9, R10,
       R11, R12, R13, R14, register_1_q, register_file_1_rd1, register_file_1_rd2;

  Multiplexer #(.width(32), .enable("false")) multiplexer_1 (
    .in0(instruction_memory_1_out_2), .in1(multiplexer_5_out), .out(multiplexer_1_out),
    .sel(control_unit_1_pcsrc));
  Register #(.width(32)) register_1 (.D(multiplexer_1_out), .Q(register_1_q), .clk(CLK), .clr(CLR));  // open: en
  Clock u_CLK (.out(CLK));
  Instruction_memory instruction_memory_1 (.A(register_1_q), .out_2(instruction_memory_1_out_2));
  Adder #(.width(32)) adder_1 (.a(register_1_q), .b(32'h4), .out(instruction_memory_1_out_2));  // open: cin, cout
  Multiplexer #(.width(4), .enable("false")) multiplexer_2 (
    .in0(instruction_memory_1_out_2[19:16]), .in1(4'b0100), .out(multiplexer_2_out),
    .sel(control_unit_1_regsrc[0]));
  Control_unit control_unit_1 (
    .Cond(instruction_memory_1_out_2[31:28]), .ALUFlags(alu_1_alu_flags),
    .Op(instruction_memory_1_out_2[27:26]), .Funct(instruction_memory_1_out_2[25:20]),
    .Rd(instruction_memory_1_out_2[15:12]), .PCSrc(control_unit_1_pcsrc), .RegWrite(control_unit_1_regwrite),
    .MemWrite(control_unit_1_memwrite), .MemtoReg(control_unit_1_memtoreg), .ALUSrc(control_unit_1_alusrc),
    .ImmSrc(control_unit_1_immsrc), .RegSrc(control_unit_1_regsrc), .ALUControl(control_unit_1_alucontrol),
    .CLK(CLK));
  Multiplexer #(.width(4), .enable("false")) multiplexer_3 (
    .in1(instruction_memory_1_out_2[15:12]), .out(multiplexer_3_out), .sel(control_unit_1_regsrc[1]));  // open: in0
  Adder #(.width(32)) adder_2 (.a(32'h4), .b(instruction_memory_1_out_2), .out(adder_2_out));  // open: cin, cout
  // Probe on R0
  Register_file register_file_1 (
    .WE3(control_unit_1_regwrite), .CLK(CLK), .CLR(CLR), .A1(multiplexer_2_out), .A2(multiplexer_3_out),
    .A3(instruction_memory_1_out_2[15:12]), .WD3(multiplexer_5_out), .R15(adder_2_out),
    .RD1(register_file_1_rd1), .RD2(register_file_1_rd2), .R0(R0), .R1(R1), .R2(R2), .R3(R3), .R4(R4),
    .R5(R5), .R6(R6), .R7(R7), .R8(R8), .R9(R9), .R10(R10), .R11(R11), .R12(R12), .R13(R13), .R14(R14));
  Extend extend_1 (.Input(instruction_memory_1_out_2), .ExtImm(extend_1_extimm), .ImmSrc(control_unit_1_immsrc));
  Multiplexer #(.width(32), .enable("false")) multiplexer_4 (
    .in0(register_file_1_rd2), .in1(extend_1_extimm), .out(multiplexer_4_out), .sel(control_unit_1_alusrc));
  ALU alu_1 (
    .ALUControl(control_unit_1_alucontrol), .B(multiplexer_4_out), .A(register_file_1_rd1),
    .Result(alu_1_result), .ALU_flags(alu_1_alu_flags));
  Data_Memory data_memory_1 (
    .ALURes(alu_1_result), .WD(register_file_1_rd2), .RD(data_memory_1_rd), .WE(control_unit_1_memwrite),
    .CLK(CLK), .CLR(CLR));
  Multiplexer #(.width(32), .enable("false")) multiplexer_5 (
    .in0(alu_1_result), .in1(data_memory_1_rd), .out(multiplexer_5_out), .sel(control_unit_1_memtoreg));
endmodule

// Zero
module AND_invert (
  input  [31:0] \input ,
  output out_2
);

  and and_1 (out_2, ~\input [0], ~\input [1], ~\input [2], ~\input [3], ~\input [4], ~\input [5], ~\input [6], ~\input [7], ~\input [8], ~\input [9], ~\input [10], ~\input [11], ~\input [12], ~\input [13], ~\input [14], ~\input [15], ~\input [16], ~\input [17], ~\input [18], ~\input [19], ~\input [20], ~\input [21], ~\input [22], ~\input [23], ~\input [24], ~\input [25], ~\input [26], ~\input [27], ~\input [28], ~\input [29], ~\input [30], ~\input [31]);  // AND_Gate
endmodule

// 31 bit \n selector
module _31_bit (
  input  [31:0] in_1,
  output _31_bit
);


  assign _31_bit = in_1[31];
endmodule

module ALU (
  input  [1:0] ALUControl,
  input  [31:0] B,
  input  [31:0] A,
  output [31:0] Result,
  output [3:0] ALU_flags
);

  wire adder_1_cout, not_2_out, xnor_1_out, xor_1_out;
  wire [31:0] adder_1_out, and_1_out, multiplexer_1_out, not_1_out, or_1_out;

  // Probe on B
  // Probe on A
  assign not_1_out = ~B;  // NOT_Gate not_1, 32 bits wide
  Multiplexer #(.width(32)) multiplexer_1 (
    .in0(B), .in1(not_1_out), .out(multiplexer_1_out), .sel(ALUControl[0]));  // open: en
  Adder #(.width(32)) adder_1 (
    .a(multiplexer_1_out), .b(A), .out(adder_1_out), .cin(ALUControl[0]), .cout(adder_1_cout));
  not not_2 (not_2_out, ALUControl[1]);
  xor xor_1 (xor_1_out, adder_1_out[31], B[31]);
  NotExactlyOne xnor_1 (.out(xnor_1_out), .in0(B[31]), .in1(A[31]), .in2(ALUControl[0]));
  // Probe on multiplexer_1_out
  // Probe on and_1_out
  assign and_1_out = B & A;  // AND_Gate and_1, 32 bits wide
  assign or_1_out = B | A;  // OR_Gate or_1, 32 bits wide
  Multiplexer #(.select(2), .width(32)) multiplexer_2 (
    .in0(adder_1_out), .in1(adder_1_out), .in2(and_1_out), .in3(or_1_out),
    .out({ALU_flags[2], Result[30:0]}), .sel(ALUControl));  // open: en
  and and_2 (ALU_flags[1], adder_1_cout, not_2_out);
  and and_3 (ALU_flags[0], not_2_out, xor_1_out, xnor_1_out);
  AND_invert and_invert_1 (.\input ({ALU_flags[2], Result[30:0]}), .out_2(ALU_flags[3]));

  assign Result[31] = ALU_flags[2];
endmodule

module Decoder (
  input  [3:0] rd,
  input  [1:0] Op,
  input  [5:0] Funct,
  output PCS,
  output RegW,
  output MemW,
  output MemtoReg,
  output ALUSrc,
  output [1:0] ImmSrc,
  output [1:0] RegSrc,
  output [1:0] ALU_Control,
  output [1:0] Flag_W
);

  wire main_decoder_1_alu_op, main_decoder_1_branch;

  Main_decoder main_decoder_1 (
    .Op(Op), .Funct_5(Funct), .Branch(main_decoder_1_branch), .Mem_to_Reg(MemtoReg), .MemW(MemW),
    .ALU_src(ALUSrc), .Imm_Src(ImmSrc), .Reg_W(RegW), .Reg_Src(RegSrc), .ALU_op(main_decoder_1_alu_op));
  ALU_decoder alu_decoder_1 (
    .in_2(Funct[4:0]), .ALUOp(main_decoder_1_alu_op), .Flag_W(Flag_W), .ALU_control(ALU_Control));  // open: No_Write
  Pc_logic pc_logic_1 (.Rd(rd), .Reg_W(RegW), .Branch(main_decoder_1_branch), .out_4(PCS));
  // Probe on main_decoder_1_alu_op
endmodule

// ALU\n decoder
module ALU_decoder (
  input  ALUOp,
  input  [4:0] in_2,
  output [1:0] Flag_W,
  output [1:0] ALU_control,
  output No_Write
);

  wire Add_out, and_2_out, and_3_out, and_4_out, and_5_out, or_3_out, Sub_out;
  wire [0:0] or_2_out;
  wire [1:0] nor_1_out, or_6_out;
  wire [1:1] And_out, or_5_out, Or_out;

  and Add (Add_out, ~in_2[1], ~in_2[2], in_2[3], ~in_2[4], ALUOp);  // AND_Gate
  and Sub (Sub_out, ~in_2[1], in_2[2], ~in_2[3], ~in_2[4], ALUOp);  // AND_Gate
  and And (And_out[1], ~in_2[1], ~in_2[2], ~in_2[3], ~in_2[4], ALUOp);  // AND_Gate
  and Or (Or_out[1], ~in_2[1], ~in_2[2], in_2[3], in_2[4], ALUOp);  // AND_Gate
  and CMP (No_Write, in_2[0], in_2[4], ~in_2[3], in_2[2], ~in_2[1], ALUOp);  // AND_Gate
  and and_2 (and_2_out, in_2[0], Add_out);
  and and_3 (and_3_out, in_2[0], Sub_out);
  and and_4 (and_4_out, in_2[0], And_out[1]);
  and and_5 (and_5_out, in_2[0], Or_out[1]);
  or or_2 (or_2_out[0], Sub_out, No_Write);
  or or_3 (or_3_out, and_2_out, and_3_out);
  or or_4 (nor_1_out[1], and_4_out, and_5_out);
  or or_5 (or_5_out[1], or_3_out, No_Write);
  nor nor_1 (nor_1_out[0], 1'b1, nor_1_out[1]);
  assign or_6_out = {And_out[1], 1'b0} | {2{Or_out[1]}};  // OR_Gate or_6, 2 bits wide
  assign Flag_W = {2{or_5_out[1]}} | nor_1_out;  // OR_Gate or_7, 2 bits wide
  assign ALU_control = {1'b0, or_2_out[0]} | or_6_out;  // OR_Gate or_8, 2 bits wide
endmodule

module Main_decoder (
  input  [1:0] Op,
  input  [5:0] Funct_5,
  output Branch,
  output Mem_to_Reg,
  output MemW,
  output ALU_src,
  output [1:0] Imm_Src,
  output Reg_W,
  output [1:0] Reg_Src,
  output ALU_op
);

  wire and_1_out, and_2_out, or_5_out, or_9_out, or_10_out;
  wire [0:0] and_3_out, and_4_out;
  wire [1:0] or_3_out;
  wire [1:1] and_5_out, or_7_out;

  and and_1 (and_1_out, ~Op[0], ~Op[1], ~Funct_5[5]);  // AND_Gate
  and and_2 (and_2_out, ~Op[0], ~Op[1], Funct_5[5]);  // AND_Gate
  and and_3 (and_3_out[0], Op[0], ~Op[1], ~Funct_5[0]);  // AND_Gate
  and and_4 (and_4_out[0], Op[0], ~Op[1], Funct_5[0]);  // AND_Gate
  and and_5 (and_5_out[1], ~Op[0], Op[1]);  // AND_Gate
  nor nor_1 (Mem_to_Reg, and_1_out, and_2_out, and_3_out[0], ~and_4_out[0], and_5_out[1]);  // NOR_Gate
  nor nor_2 (Branch, and_1_out, and_2_out, and_3_out[0], and_4_out[0], ~and_5_out[1]);  // NOR_Gate
  nor nor_3 (MemW, and_1_out, and_2_out, ~and_3_out[0], and_4_out[0], and_5_out[1]);  // NOR_Gate
  or or_1 (ALU_src, ~and_1_out, and_2_out, and_3_out[0], and_4_out[0], and_5_out[1]);  // OR_Gate
  assign Imm_Src = or_3_out | {and_5_out[1], 1'b0};  // OR_Gate or_2, 2 bits wide
  assign or_3_out = {1'b0, and_3_out[0]} | {1'b0, and_4_out[0]};  // OR_Gate or_3, 2 bits wide
  or or_4 (Reg_W, and_1_out, and_2_out, and_4_out[0], ~or_5_out);  // OR_Gate
  or or_5 (or_5_out, and_3_out[0], and_5_out[1]);
  assign Reg_Src = {or_7_out[1], 1'b0} | {and_3_out[0], 1'b0} | {1'b0, and_5_out[1]};  // OR_Gate or_6, 2 bits wide
  or or_7 (or_7_out[1], and_2_out, and_4_out[0]);
  or or_8 (ALU_op, or_10_out, ~or_9_out);  // OR_Gate
  or or_9 (or_9_out, and_3_out[0], and_4_out[0], and_5_out[1]);
  or or_10 (or_10_out, and_1_out, and_2_out);
endmodule

module Pc_logic (
  input  [3:0] Rd,
  input  Reg_W,
  input  Branch,
  output out_4
);

  wire and_1_out;

  and and_1 (and_1_out, Rd[0], Rd[1], Rd[2], Rd[3], Reg_W);
  or or_1 (out_4, and_1_out, Branch);
endmodule

module Conditinal_Logic (
  input  PCS,
  input  RegW,
  input  MemW,
  input  [1:0] FlagW,
  input  [3:0] Cond,
  input  CLK,
  input  [3:0] ALUFlags,
  output PCSrc,
  output RegWrite,
  output MemWrite
);

  wire condition_check_1_condex;
  wire [1:0] and_1_out, bit_extender_1_out, register_1_q, register_2_q;

  Register #(.width(2)) register_1 (.D(ALUFlags[3:2]), .en(1'b1), .Q(register_1_q), .clk(CLK), .clr(and_1_out[1]));
  Register #(.width(2)) register_2 (.D(ALUFlags[1:0]), .en(1'b1), .Q(register_2_q), .clk(CLK), .clr(and_1_out[0]));
  assign bit_extender_1_out = {{1{condition_check_1_condex}}, condition_check_1_condex};  // Bit_Extender bit_extender_1
  assign and_1_out = FlagW & bit_extender_1_out;  // AND_Gate and_1, 2 bits wide
  Condition_check condition_check_1 (
    .CondEx(condition_check_1_condex), .Flags_2_3(register_1_q), .Flags_0_1(register_2_q), .Cond(Cond));
  and and_2 (PCSrc, PCS, condition_check_1_condex);
  and and_3 (RegWrite, RegW, condition_check_1_condex);
  and and_4 (MemWrite, MemW, condition_check_1_condex);
endmodule

module Condition_check (
  input  [1:0] Flags_2_3,
  input  [1:0] Flags_0_1,
  input  [3:0] Cond,
  output CondEx
);

  wire EQ_out, NE_out;

  and EQ (EQ_out, ~Cond[0], ~Cond[1], ~Cond[2], ~Cond[3], ~Flags_0_1[0], ~Flags_0_1[1], ~Flags_2_3[0], Flags_2_3[1]);  // AND_Gate
  and NE (NE_out, Cond[0], ~Cond[1], ~Cond[2], ~Cond[3], ~Flags_0_1[0], ~Flags_0_1[1], ~Flags_2_3[0], ~Flags_2_3[1]);  // AND_Gate
  or or_1 (CondEx, EQ_out, NE_out);
endmodule

// Control \n unit
module Control_unit (
  input  CLK,
  input  [3:0] Cond,
  input  [3:0] ALUFlags,
  input  [1:0] Op,
  input  [5:0] Funct,
  input  [3:0] Rd,
  output PCSrc,
  output RegWrite,
  output MemWrite,
  output MemtoReg,
  output ALUSrc,
  output [1:0] ImmSrc,
  output [1:0] RegSrc,
  output [1:0] ALUControl
);

  wire decoder_1_memw, decoder_1_pcs, decoder_1_regw;
  wire [1:0] decoder_1_flag_w;

  Decoder decoder_1 (
    .rd(Rd), .Op(Op), .Funct(Funct), .PCS(decoder_1_pcs), .RegW(decoder_1_regw), .MemW(decoder_1_memw),
    .MemtoReg(MemtoReg), .ALUSrc(ALUSrc), .ImmSrc(ImmSrc), .RegSrc(RegSrc), .ALU_Control(ALUControl),
    .Flag_W(decoder_1_flag_w));
  Conditinal_Logic conditinal_logic_1 (
    .PCS(decoder_1_pcs), .RegW(decoder_1_regw), .MemW(decoder_1_memw), .FlagW(decoder_1_flag_w), .Cond(Cond),
    .CLK(CLK), .ALUFlags(ALUFlags), .PCSrc(PCSrc), .RegWrite(RegWrite), .MemWrite(MemWrite));
endmodule

module Data_Memory (
  input  [31:0] ALURes,
  input  [31:0] WD,
  input  WE,
  input  CLK,
  input  CLR,
  output [31:0] RD
);

  wire not_1_out;

  not not_1 (not_1_out, WE);
  RAM #(.dataWidth(32), .bus("separate")) ram_1 (
    .addr(ALURes[7:0]), .din(WD), .data(RD), .str(WE), .clk(CLK), .ld(not_1_out), .clr(CLR));  // open: sel
endmodule

// Register \n file
module Register_file (
  input  WE3,
  input  CLK,
  input  CLR,
  input  [3:0] A1,
  input  [3:0] A2,
  input  [3:0] A3,
  input  [31:0] WD3,
  input  [31:0] R15,
  output [31:0] R0,
  output [31:0] R1,
  output [31:0] R2,
  output [31:0] R3,
  output [31:0] R4,
  output [31:0] R5,
  output [31:0] R6,
  output [31:0] R7,
  output [31:0] R8,
  output [31:0] R9,
  output [31:0] R10,
  output [31:0] RD1,
  output [31:0] R11,
  output [31:0] R12,
  output [31:0] RD2,
  output [31:0] R13,
  output [31:0] R14
);

  wire and_1_out, and_2_out, and_3_out, and_4_out, and_5_out, and_6_out, and_7_out, and_8_out, and_9_out,
       and_10_out, and_11_out, and_12_out, and_13_out, and_14_out, and_15_out, decoder_1_out0,
       decoder_1_out1, decoder_1_out2, decoder_1_out3, decoder_1_out4, decoder_1_out5, decoder_1_out6,
       decoder_1_out7, decoder_1_out8, decoder_1_out9, decoder_1_out10, decoder_1_out11, decoder_1_out12,
       decoder_1_out13, decoder_1_out14;

  Decoder_part #(.select(4), .enable("false")) decoder_1 (
    .out0(decoder_1_out0), .out1(decoder_1_out1), .out2(decoder_1_out2), .out3(decoder_1_out3),
    .out4(decoder_1_out4), .out5(decoder_1_out5), .out6(decoder_1_out6), .out7(decoder_1_out7),
    .out8(decoder_1_out8), .out9(decoder_1_out9), .out10(decoder_1_out10), .out11(decoder_1_out11),
    .out12(decoder_1_out12), .out13(decoder_1_out13), .out14(decoder_1_out14), .sel(A1));  // open: out15
  and and_1 (and_1_out, WE3, decoder_1_out0);
  and and_2 (and_2_out, WE3, decoder_1_out1);
  and and_3 (and_3_out, WE3, decoder_1_out2);
  and and_4 (and_4_out, WE3, decoder_1_out3);
  and and_5 (and_5_out, WE3, decoder_1_out4);
  and and_6 (and_6_out, WE3, decoder_1_out5);
  and and_7 (and_7_out, WE3, decoder_1_out6);
  and and_8 (and_8_out, WE3, decoder_1_out7);
  and and_9 (and_9_out, WE3, decoder_1_out8);
  and and_10 (and_10_out, WE3, decoder_1_out9);
  and and_11 (and_11_out, WE3, decoder_1_out10);
  and and_12 (and_12_out, WE3, decoder_1_out11);
  and and_13 (and_13_out, WE3, decoder_1_out12);
  and and_14 (and_14_out, WE3, decoder_1_out13);
  and and_15 (and_15_out, WE3, decoder_1_out14);
  Register #(.width(32)) u_R0 (.D(WD3), .en(and_1_out), .Q(R0), .clk(CLK), .clr(CLR));
  Register #(.width(32)) u_R1 (.D(WD3), .en(and_2_out), .Q(R1), .clk(CLK), .clr(CLR));
  Register #(.width(32)) u_R2 (.D(WD3), .en(and_3_out), .Q(R2), .clk(CLK), .clr(CLR));
  Register #(.width(32)) u_R3 (.D(WD3), .en(and_4_out), .Q(R3), .clk(CLK), .clr(CLR));
  Register #(.width(32)) u_R4 (.D(WD3), .en(and_5_out), .Q(R4), .clk(CLK), .clr(CLR));
  Register #(.width(32)) u_R5 (.D(WD3), .en(and_6_out), .Q(R5), .clk(CLK), .clr(CLR));
  Register #(.width(32)) u_R6 (.D(WD3), .en(and_7_out), .Q(R6), .clk(CLK), .clr(CLR));
  Register #(.width(32)) u_R7 (.D(WD3), .en(and_8_out), .Q(R7), .clk(CLK), .clr(CLR));
  Register #(.width(32)) u_R8 (.D(WD3), .en(and_9_out), .Q(R8), .clk(CLK), .clr(CLR));
  Register #(.width(32)) u_R9 (.D(WD3), .en(and_10_out), .Q(R9), .clk(CLK), .clr(CLR));
  Register #(.width(32)) u_R10 (.D(WD3), .en(and_11_out), .Q(R10), .clk(CLK), .clr(CLR));
  Register #(.width(32)) u_R11 (.D(WD3), .en(and_12_out), .Q(R11), .clk(CLK), .clr(CLR));
  Register #(.width(32)) u_R12 (.D(WD3), .en(and_13_out), .Q(R12), .clk(CLK), .clr(CLR));
  Register #(.width(32)) u_R13 (.D(WD3), .en(and_14_out), .Q(R13), .clk(CLK), .clr(CLR));
  Register #(.width(32)) u_R14 (.D(WD3), .en(and_15_out), .Q(R14), .clk(CLK), .clr(CLR));
  Multiplexer #(.select(4), .width(32), .enable("false")) multiplexer_1 (
    .in0(R0), .in1(R1), .in2(R2), .in3(R3), .in4(R4), .in5(R5), .in6(R6), .in7(R7), .in8(R8), .in9(R9),
    .in10(R10), .in11(R11), .in12(R12), .in13(R13), .in14(R14), .in15(R15), .out(RD1), .sel(A2));
  Multiplexer #(.select(4), .width(32), .enable("false")) multiplexer_2 (
    .in0(R0), .in1(R1), .in2(R2), .in3(R3), .in4(R4), .in5(R5), .in6(R6), .in7(R7), .in8(R8), .in9(R9),
    .in10(R10), .in11(R11), .in12(R12), .in13(R13), .in14(R14), .in15(R15), .out(RD2), .sel(A3));
endmodule

// Instruction\nmemory
module Instruction_memory (
  input  [31:0] A,
  output [31:0] out_2
);

  wire [7:0] undriven;
  wire [31:0] rom_2_data, rom_3_data, rom_4_data, undriven_2;

  ROM #(.dataWidth(32)) rom_1 (.addr(A[9:2]), .data(out_2));  // open: sel
  ROM #(.dataWidth(32)) rom_2 (.addr(undriven), .data(rom_2_data));  // open: sel
  ROM #(.dataWidth(32)) rom_3 (.addr(undriven), .data(rom_3_data));  // open: sel
  ROM #(.dataWidth(32)) rom_4 (.addr(undriven), .data(rom_4_data));  // open: sel
  Multiplexer #(.select(2), .width(32), .enable("false")) multiplexer_1 (
    .in0(undriven_2), .in1(rom_2_data), .in2(rom_3_data), .in3(rom_4_data));  // open: out, sel

  // Notes on the sheet:
  //   contents of rom_1 (hex, n*v repeats v):
  //   e280000f
endmodule

module Extend (
  input  [31:0] Input,
  input  [1:0] ImmSrc,
  output [31:0] ExtImm
);

  wire [31:0] bit_extender_1_out, bit_extender_2_out, bit_extender_3_out;

  assign bit_extender_1_out = {{24{1'b0}}, Input[7:0]};  // Bit_Extender bit_extender_1
  assign bit_extender_2_out = {{20{1'b0}}, Input[11:0]};  // Bit_Extender bit_extender_2
  assign bit_extender_3_out = {{8{Input[23]}}, Input[23:0]};  // Bit_Extender bit_extender_3
  Multiplexer #(.select(2), .width(32), .enable("false")) multiplexer_1 (
    .in0(bit_extender_1_out), .in1(bit_extender_2_out), .in2(bit_extender_3_out), .out(ExtImm), .sel(ImmSrc));  // open: in3
endmodule
